// Digital circuit somador4bits.dig as structural Verilog
module somador4bits (
  input  in_1,
  input  in_2,
  input  in_3,
  input  in_4,
  input  in_5,
  input  in_6,
  input  in_7,
  input  in_8,
  output out_9,
  output out_10,
  output out_11,
  output out_12
);

  wire somador_1_c_out, somador_2_c_out, somador_3_c_out, somador_4_c_out;

  somador somador_1 (.A(in_5), .B(in_1), .C_in(somador_2_c_out), .S(out_10), .C_out(somador_1_c_out));
  LED OVERFLOW (.in(somador_1_c_out));
  somador somador_2 (.A(in_6), .B(in_2), .C_in(somador_3_c_out), .S(out_9), .C_out(somador_2_c_out));
  Seven_Seg_Hex seven_seg_hex_1 (.d({out_10, out_9, out_11, out_12}), .dp(1'b0));
  somador somador_3 (.A(in_7), .B(in_3), .C_in(somador_4_c_out), .S(out_11), .C_out(somador_3_c_out));
  somador somador_4 (.A(in_8), .B(in_4), .C_in(1'b0), .S(out_12), .C_out(somador_4_c_out));
endmodule
